// Logisim project ЭВМ1.circ as structural Verilog
module \СКНФ  (
);

  wire and_1_out, and_2_out, and_3_out, and_4_out, and_5_out, and_6_out, and_7_out, not_1_out, not_2_out,
       not_3_out, not_4_out, not_5_out, not_6_out, not_7_out, not_8_out, not_9_out, not_10_out, not_11_out,
       not_12_out, not_13_out, not_14_out, not_15_out, not_16_out, not_17_out, not_18_out, or_1_out,
       or_2_out, or_3_out, or_4_out, or_5_out, or_6_out, or_7_out, or_8_out, or_9_out, or_10_out, or_11_out,
       or_12_out, or_13_out, or_14_out, or_15_out, or_16_out, or_17_out, or_18_out, or_19_out, or_20_out,
       or_21_out, or_22_out, or_23_out, or_24_out, x0_out, x1_out, x2_out, x3_out;

  Clock #(.highDuration(8), .lowDuration(8)) x3 (.out(x3_out));
  Clock #(.highDuration(4), .lowDuration(4)) x2 (.out(x2_out));
  Clock #(.highDuration(2), .lowDuration(2)) x1 (.out(x1_out));
  Clock x0 (.out(x0_out));
  not not_1 (not_1_out, x0_out);
  not not_2 (not_2_out, x1_out);
  not not_3 (not_3_out, x2_out);
  not not_4 (not_4_out, x3_out);
  not not_5 (not_5_out, x0_out);
  not not_6 (not_6_out, x3_out);
  not not_7 (not_7_out, x2_out);
  not not_8 (not_8_out, x3_out);
  not not_9 (not_9_out, x0_out);
  not not_10 (not_10_out, x2_out);
  not not_11 (not_11_out, x3_out);
  not not_12 (not_12_out, x1_out);
  not not_13 (not_13_out, x2_out);
  not not_14 (not_14_out, x3_out);
  not not_15 (not_15_out, x0_out);
  not not_16 (not_16_out, x1_out);
  not not_17 (not_17_out, x2_out);
  not not_18 (not_18_out, x3_out);
  or or_1 (or_1_out, x0_out, x1_out);
  or or_2 (or_2_out, x2_out, x3_out);
  or or_3 (or_3_out, not_1_out, not_2_out);
  or or_4 (or_4_out, not_3_out, x3_out);
  or or_5 (or_5_out, x0_out, x1_out);
  or or_6 (or_6_out, x2_out, not_4_out);
  or or_7 (or_7_out, not_5_out, x1_out);
  or or_8 (or_8_out, x2_out, not_6_out);
  or or_9 (or_9_out, x0_out, x1_out);
  or or_10 (or_10_out, not_7_out, not_8_out);
  or or_11 (or_11_out, not_9_out, x1_out);
  or or_12 (or_12_out, not_10_out, not_11_out);
  or or_13 (or_13_out, x0_out, not_12_out);
  or or_14 (or_14_out, not_13_out, not_14_out);
  or or_15 (or_15_out, not_15_out, not_16_out);
  or or_16 (or_16_out, not_17_out, not_18_out);
  or or_17 (or_17_out, or_1_out, or_2_out);
  or or_18 (or_18_out, or_3_out, or_4_out);
  or or_19 (or_19_out, or_5_out, or_6_out);
  or or_20 (or_20_out, or_7_out, or_8_out);
  or or_21 (or_21_out, or_9_out, or_10_out);
  or or_22 (or_22_out, or_11_out, or_12_out);
  or or_23 (or_23_out, or_13_out, or_14_out);
  or or_24 (or_24_out, or_15_out, or_16_out);
  and and_1 (and_1_out, or_17_out, or_18_out);
  and and_2 (and_2_out, or_19_out, or_20_out);
  and and_3 (and_3_out, or_21_out, or_22_out);
  and and_4 (and_4_out, or_23_out, or_24_out);
  and and_5 (and_5_out, and_1_out, and_2_out);
  and and_6 (and_6_out, and_3_out, and_4_out);
  and and_7 (and_7_out, and_5_out, and_6_out);
  LED led_1 (.in(and_7_out));
endmodule

module \МДНФ  (
);

  wire and_1_out, and_2_out, and_3_out, and_4_out, and_5_out, and_6_out, and_7_out, not_1_out, not_2_out,
       not_3_out, not_4_out, not_5_out, not_6_out, not_7_out, or_1_out, or_2_out, or_3_out, x0_out, x1_out,
       x2_out, x3_out;

  Clock #(.highDuration(8), .lowDuration(8)) x3 (.out(x3_out));
  Clock #(.highDuration(4), .lowDuration(4)) x2 (.out(x2_out));
  Clock #(.highDuration(2), .lowDuration(2)) x1 (.out(x1_out));
  Clock x0 (.out(x0_out));
  not not_1 (not_1_out, x0_out);
  not not_2 (not_2_out, x1_out);
  and and_1 (and_1_out, not_2_out, x0_out);
  and and_2 (and_2_out, x2_out, not_3_out);
  not not_3 (not_3_out, x1_out);
  and and_3 (and_3_out, x1_out, not_1_out);
  not not_4 (not_4_out, x3_out);
  not not_5 (not_5_out, x3_out);
  not not_6 (not_6_out, x3_out);
  not not_7 (not_7_out, x2_out);
  and and_4 (and_4_out, and_1_out, not_4_out);
  and and_5 (and_5_out, and_2_out, not_5_out);
  and and_6 (and_6_out, and_3_out, not_6_out);
  and and_7 (and_7_out, not_7_out, x1_out);
  or or_1 (or_1_out, and_4_out, and_5_out);
  or or_2 (or_2_out, and_6_out, and_7_out);
  or or_3 (or_3_out, or_1_out, or_2_out);
  LED led_1 (.in(or_3_out));
endmodule
