// Logisim project ЭВМ2.circ as structural Verilog
module RStrigger (
  input  in_1,
  input  in_2,
  input  in_3,
  input  in_4,
  output out_5,
  output out_6
);

  wire and_1_out, and_2_out;

  and and_1 (and_1_out, in_1, in_2);
  and and_2 (and_2_out, in_2, in_3);
  nor nor_1 (out_5, and_1_out, out_6);
  nor nor_2 (out_6, out_5, in_4, and_2_out);
endmodule

module Counter (
);

  wire clock_1_out, undriven, undriven_2, undriven_3;

  Clock clock_1 (.out(clock_1_out));
  Clock clock_2 (.out(clock_1_out));
  LED led_1 (.in(undriven));
  Ttrigger ttrigger_1 ();
  Ttrigger ttrigger_2 ();
  LED led_2 (.in(undriven_2));
  Ttrigger ttrigger_3 ();
  LED led_3 (.in(undriven_3));
endmodule

module root (
  input  bit0,
  input  bit1,
  input  bit2,
  input  bit3,
  input  bit4,
  input  bit5,
  input  bit6,
  input  bit7,
  output out_9,
  output out_10,
  output out_11,
  output out_12
);

  wire if_1_out_18, if_1_out_19, if_1_out_20, if_1_out_21, if_1_out_22, if_1_out_23, if_2_out_18,
       if_2_out_19, if_2_out_20, if_2_out_21, if_2_out_22, if_2_out_23, if_3_out_18, if_3_out_19,
       if_3_out_20, if_3_out_21, if_3_out_22, if_3_out_23, if_3_out_24, if_3_out_25, subtractor_1_out_17,
       subtractor_1_out_18, subtractor_1_out_19, subtractor_1_out_20, subtractor_1_out_21,
       subtractor_1_out_22, subtractor_1_out_25, subtractor_2_out_17, subtractor_2_out_18,
       subtractor_2_out_19, subtractor_2_out_20, subtractor_2_out_21, subtractor_2_out_22,
       subtractor_2_out_25, subtractor_3_out_17, subtractor_3_out_18, subtractor_3_out_19,
       subtractor_3_out_20, subtractor_3_out_21, subtractor_3_out_22, subtractor_3_out_25,
       subtractor_4_out_25, x4p1_1_out_9, x4p1_1_out_10, x4p1_1_out_11, x4p1_1_out_12, x4p1_1_out_13,
       x4p1_1_out_14, x4p1_1_out_15, x4p1_1_out_16, x4p1_2_out_9, x4p1_2_out_10, x4p1_2_out_11,
       x4p1_2_out_12, x4p1_2_out_13, x4p1_2_out_14, x4p1_2_out_15, x4p1_2_out_16, x4p1_3_out_9,
       x4p1_3_out_10, x4p1_3_out_11, x4p1_3_out_12, x4p1_3_out_13, x4p1_3_out_14, x4p1_3_out_15,
       x4p1_3_out_16, x4p1_4_out_9, x4p1_4_out_10, x4p1_4_out_11, x4p1_4_out_12, x4p1_4_out_13,
       x4p1_4_out_14, x4p1_4_out_15, x4p1_4_out_16;

  x4p1 x4p1_1 (
    .out_9(x4p1_1_out_9), .out_10(x4p1_1_out_10), .out_11(x4p1_1_out_11), .out_12(x4p1_1_out_12),
    .out_13(x4p1_1_out_13), .out_14(x4p1_1_out_14), .out_15(x4p1_1_out_15), .out_16(x4p1_1_out_16));  // open: bin0_1, bin1_1, bin2_1, bin3_1, bin4_1, bin5_1, bin6_1, bin7_1, out_17
  subtractor subtractor_1 (
    .bin0_1(bit6), .bin0_2(x4p1_1_out_9), .bin1_1(bit7), .bin1_2(x4p1_1_out_10), .bin2_2(x4p1_1_out_11),
    .bin3_2(x4p1_1_out_12), .bin4_2(x4p1_1_out_13), .bin5_2(x4p1_1_out_14), .bin6_2(x4p1_1_out_15),
    .bin7_2(x4p1_1_out_16), .out_17(subtractor_1_out_17), .out_18(subtractor_1_out_18),
    .out_19(subtractor_1_out_19), .out_20(subtractor_1_out_20), .out_21(subtractor_1_out_21),
    .out_22(subtractor_1_out_22), .out_25(subtractor_1_out_25));  // open: bin2_1, bin3_1, bin4_1, bin5_1, bin6_1, bin7_1, out_23, out_24
  not not_1 (out_12, subtractor_1_out_25);
  \if  if_1 (
    .bin0_1(bit4), .bin0_2(bit4), .bin1_1(bit5), .bin1_2(bit5), .bin2_1(bit6), .bin2_2(subtractor_1_out_17),
    .bin3_1(bit7), .bin3_2(subtractor_1_out_18), .bin4_2(subtractor_1_out_19), .bin5_2(subtractor_1_out_20),
    .bin6_2(subtractor_1_out_21), .bin7_2(subtractor_1_out_22), .in_17(out_12), .out_18(if_1_out_18),
    .out_19(if_1_out_19), .out_20(if_1_out_20), .out_21(if_1_out_21), .out_22(if_1_out_22),
    .out_23(if_1_out_23));  // open: bin4_1, bin5_1, bin6_1, bin7_1, out_24, out_25
  x4p1 x4p1_2 (
    .bin0_1(out_12), .out_9(x4p1_2_out_9), .out_10(x4p1_2_out_10), .out_11(x4p1_2_out_11),
    .out_12(x4p1_2_out_12), .out_13(x4p1_2_out_13), .out_14(x4p1_2_out_14), .out_15(x4p1_2_out_15),
    .out_16(x4p1_2_out_16));  // open: bin1_1, bin2_1, bin3_1, bin4_1, bin5_1, bin6_1, bin7_1, out_17
  subtractor subtractor_2 (
    .bin0_1(if_1_out_18), .bin0_2(x4p1_2_out_9), .bin1_1(if_1_out_19), .bin1_2(x4p1_2_out_10),
    .bin2_1(if_1_out_20), .bin2_2(x4p1_2_out_11), .bin3_1(if_1_out_21), .bin3_2(x4p1_2_out_12),
    .bin4_1(if_1_out_22), .bin4_2(x4p1_2_out_13), .bin5_1(if_1_out_23), .bin5_2(x4p1_2_out_14),
    .bin6_2(x4p1_2_out_15), .bin7_2(x4p1_2_out_16), .out_17(subtractor_2_out_17),
    .out_18(subtractor_2_out_18), .out_19(subtractor_2_out_19), .out_20(subtractor_2_out_20),
    .out_21(subtractor_2_out_21), .out_22(subtractor_2_out_22), .out_25(subtractor_2_out_25));  // open: bin6_1, bin7_1, out_23, out_24
  not not_2 (out_11, subtractor_2_out_25);
  \if  if_2 (
    .bin0_1(bit2), .bin0_2(bit3), .bin1_1(bit3), .bin1_2(bit2), .bin2_1(if_1_out_18),
    .bin2_2(subtractor_2_out_17), .bin3_1(if_1_out_19), .bin3_2(subtractor_2_out_18), .bin4_1(if_1_out_20),
    .bin4_2(subtractor_2_out_19), .bin5_1(if_1_out_21), .bin5_2(subtractor_2_out_20),
    .bin6_2(subtractor_2_out_21), .bin7_2(subtractor_2_out_22), .in_17(out_11), .out_18(if_2_out_18),
    .out_19(if_2_out_19), .out_20(if_2_out_20), .out_21(if_2_out_21), .out_22(if_2_out_22),
    .out_23(if_2_out_23));  // open: bin6_1, bin7_1, out_24, out_25
  x4p1 x4p1_3 (
    .bin0_1(out_11), .bin1_1(out_12), .out_9(x4p1_3_out_9), .out_10(x4p1_3_out_10), .out_11(x4p1_3_out_11),
    .out_12(x4p1_3_out_12), .out_13(x4p1_3_out_13), .out_14(x4p1_3_out_14), .out_15(x4p1_3_out_15),
    .out_16(x4p1_3_out_16));  // open: bin2_1, bin3_1, bin4_1, bin5_1, bin6_1, bin7_1, out_17
  subtractor subtractor_3 (
    .bin0_1(if_2_out_18), .bin0_2(x4p1_3_out_9), .bin1_1(if_2_out_19), .bin1_2(x4p1_3_out_10),
    .bin2_1(if_2_out_20), .bin2_2(x4p1_3_out_11), .bin3_1(if_2_out_21), .bin3_2(x4p1_3_out_12),
    .bin4_1(if_2_out_22), .bin4_2(x4p1_3_out_13), .bin5_1(if_2_out_23), .bin5_2(x4p1_3_out_14),
    .bin6_2(x4p1_3_out_15), .bin7_2(x4p1_3_out_16), .out_17(subtractor_3_out_17),
    .out_18(subtractor_3_out_18), .out_19(subtractor_3_out_19), .out_20(subtractor_3_out_20),
    .out_21(subtractor_3_out_21), .out_22(subtractor_3_out_22), .out_25(subtractor_3_out_25));  // open: bin6_1, bin7_1, out_23, out_24
  not not_3 (out_10, subtractor_3_out_25);
  \if  if_3 (
    .bin0_1(bit0), .bin0_2(bit0), .bin1_1(bit1), .bin1_2(bit1), .bin2_1(if_2_out_18),
    .bin2_2(subtractor_3_out_17), .bin3_1(if_2_out_19), .bin3_2(subtractor_3_out_18), .bin4_1(if_2_out_20),
    .bin4_2(subtractor_3_out_19), .bin5_1(if_2_out_21), .bin5_2(subtractor_3_out_20), .bin6_1(if_2_out_22),
    .bin6_2(subtractor_3_out_21), .bin7_1(if_2_out_23), .bin7_2(subtractor_3_out_22), .in_17(out_10),
    .out_18(if_3_out_18), .out_19(if_3_out_19), .out_20(if_3_out_20), .out_21(if_3_out_21),
    .out_22(if_3_out_22), .out_23(if_3_out_23), .out_24(if_3_out_24), .out_25(if_3_out_25));
  x4p1 x4p1_4 (
    .bin0_1(out_10), .bin1_1(out_11), .bin2_1(out_12), .out_9(x4p1_4_out_9), .out_10(x4p1_4_out_10),
    .out_11(x4p1_4_out_11), .out_12(x4p1_4_out_12), .out_13(x4p1_4_out_13), .out_14(x4p1_4_out_14),
    .out_15(x4p1_4_out_15), .out_16(x4p1_4_out_16));  // open: bin3_1, bin4_1, bin5_1, bin6_1, bin7_1, out_17
  subtractor subtractor_4 (
    .bin0_1(if_3_out_18), .bin0_2(x4p1_4_out_9), .bin1_1(if_3_out_19), .bin1_2(x4p1_4_out_10),
    .bin2_1(if_3_out_20), .bin2_2(x4p1_4_out_11), .bin3_1(if_3_out_21), .bin3_2(x4p1_4_out_12),
    .bin4_1(if_3_out_22), .bin4_2(x4p1_4_out_13), .bin5_1(if_3_out_23), .bin5_2(x4p1_4_out_14),
    .bin6_1(if_3_out_24), .bin6_2(x4p1_4_out_15), .bin7_1(if_3_out_25), .bin7_2(x4p1_4_out_16),
    .out_25(subtractor_4_out_25));  // open: out_17, out_18, out_19, out_20, out_21, out_22, out_23, out_24
  not not_4 (out_9, subtractor_4_out_25);
endmodule

module summator (
  input  bin0_1,
  input  bin0_2,
  input  in_3,
  input  bin1_2,
  input  bin2_1,
  input  bin2_2,
  input  bin3_1,
  input  bin3_2,
  input  bin4_1,
  input  bin4_2,
  input  bin5_1,
  input  bin5_2,
  input  bin6_1,
  input  bin6_2,
  input  bin7_1,
  input  bin7_2,
  input  in_17,
  input  in_18,
  output out_19,
  output out_20,
  output out_21,
  output out_22,
  output out_23,
  output out_24,
  output out_25,
  output out_26,
  output out_27
);

  wire summator_3_1_out_5, summator_3_2_out_5, summator_3_3_out_5, summator_3_4_out_5, summator_3_5_out_5,
       summator_3_6_out_5, summator_3_7_out_5, summator_3_8_out_5;

  summator_3 summator_3_1 (.in_1(bin0_1), .in_2(bin0_2), .in_3(1'b0), .out_4(out_19), .out_5(summator_3_1_out_5));
  summator_3 summator_3_2 (
    .in_1(summator_3_1_out_5), .in_2(bin1_2), .in_3(in_3), .out_4(out_20), .out_5(summator_3_2_out_5));
  summator_3 summator_3_3 (
    .in_1(summator_3_2_out_5), .in_2(bin2_2), .in_3(bin2_1), .out_4(out_21), .out_5(summator_3_3_out_5));
  summator_3 summator_3_4 (
    .in_1(summator_3_3_out_5), .in_2(bin3_2), .in_3(bin3_1), .out_4(out_22), .out_5(summator_3_4_out_5));
  summator_3 summator_3_5 (
    .in_1(summator_3_4_out_5), .in_2(bin4_2), .in_3(bin4_1), .out_4(out_23), .out_5(summator_3_5_out_5));
  summator_3 summator_3_6 (
    .in_1(summator_3_5_out_5), .in_2(bin5_2), .in_3(bin5_1), .out_4(out_24), .out_5(summator_3_6_out_5));
  summator_3 summator_3_7 (
    .in_1(summator_3_6_out_5), .in_2(bin6_2), .in_3(bin6_1), .out_4(out_25), .out_5(summator_3_7_out_5));
  summator_3 summator_3_8 (
    .in_1(summator_3_7_out_5), .in_2(bin7_1), .in_3(bin7_2), .out_4(out_26), .out_5(summator_3_8_out_5));
  summator_3 summator_3_9 (.in_1(summator_3_8_out_5), .in_2(in_17), .in_3(in_18), .out_4(out_27));  // open: out_5
endmodule

module summator_3 (
  input  in_1,
  input  in_2,
  input  in_3,
  output out_4,
  output out_5
);

  wire and_1_out, and_2_out, and_3_out, xor_1_out;

  xor xor_1 (xor_1_out, in_1, in_2);
  and and_1 (and_1_out, in_1, in_2);
  and and_2 (and_2_out, in_1, in_3);
  and and_3 (and_3_out, in_2, in_3);
  xor xor_2 (out_4, xor_1_out, in_3);
  or or_1 (out_5, and_1_out, and_2_out, and_3_out);
endmodule

module subtractor (
  input  bin0_1,
  input  bin0_2,
  input  bin1_1,
  input  bin1_2,
  input  bin2_1,
  input  bin2_2,
  input  bin3_1,
  input  bin3_2,
  input  bin4_1,
  input  bin4_2,
  input  bin5_1,
  input  bin5_2,
  input  bin6_1,
  input  bin6_2,
  input  bin7_1,
  input  bin7_2,
  output out_17,
  output out_18,
  output out_19,
  output out_20,
  output out_21,
  output out_22,
  output out_23,
  output out_24,
  output out_25
);

  wire not_1_out, not_2_out, not_3_out, not_4_out, not_5_out, not_6_out, not_7_out, not_8_out,
       summator_1_out_19, summator_1_out_20, summator_1_out_21, summator_1_out_22, summator_1_out_23,
       summator_1_out_24, summator_1_out_25, summator_1_out_26, summator_1_out_27;

  not not_1 (not_1_out, bin0_2);
  not not_2 (not_2_out, bin1_2);
  not not_3 (not_3_out, bin2_2);
  not not_4 (not_4_out, bin3_2);
  not not_5 (not_5_out, bin4_2);
  not not_6 (not_6_out, bin5_2);
  not not_7 (not_7_out, bin6_2);
  not not_8 (not_8_out, bin7_2);
  summator summator_1 (
    .bin0_1(not_1_out), .in_3(not_2_out), .bin2_1(not_3_out), .bin3_1(not_4_out), .bin4_1(not_5_out),
    .bin5_1(not_6_out), .bin6_1(not_7_out), .bin7_1(not_8_out), .in_17(1'b1), .bin0_2(1'b1),
    .out_19(summator_1_out_19), .out_20(summator_1_out_20), .out_21(summator_1_out_21),
    .out_22(summator_1_out_22), .out_23(summator_1_out_23), .out_24(summator_1_out_24),
    .out_25(summator_1_out_25), .out_26(summator_1_out_26), .out_27(summator_1_out_27));  // open: bin1_2, bin2_2, bin3_2, bin4_2, bin5_2, bin6_2, bin7_2, in_18
  summator summator_2 (
    .bin0_1(summator_1_out_19), .in_3(summator_1_out_20), .bin2_1(summator_1_out_21),
    .bin3_1(summator_1_out_22), .bin4_1(summator_1_out_23), .bin5_1(summator_1_out_24),
    .bin6_1(summator_1_out_25), .bin7_1(summator_1_out_26), .in_17(summator_1_out_27), .bin0_2(bin0_1),
    .bin1_2(bin1_1), .bin2_2(bin2_1), .bin3_2(bin3_1), .bin4_2(bin4_1), .bin5_2(bin5_1), .bin6_2(bin6_1),
    .bin7_2(bin7_1), .out_19(out_17), .out_20(out_18), .out_21(out_19), .out_22(out_20), .out_23(out_21),
    .out_24(out_22), .out_25(out_23), .out_26(out_24), .out_27(out_25));  // open: in_18
endmodule

module \if  (
  input  bin0_1,
  input  bin0_2,
  input  bin1_1,
  input  bin1_2,
  input  bin2_1,
  input  bin2_2,
  input  bin3_1,
  input  bin3_2,
  input  bin4_1,
  input  bin4_2,
  input  bin5_1,
  input  bin5_2,
  input  bin6_1,
  input  bin6_2,
  input  bin7_1,
  input  bin7_2,
  input  in_17,
  output out_18,
  output out_19,
  output out_20,
  output out_21,
  output out_22,
  output out_23,
  output out_24,
  output out_25
);

  wire and_1_out, and_2_out, and_3_out, and_4_out, and_5_out, and_6_out, and_7_out, and_8_out, and_9_out,
       and_10_out, and_11_out, and_12_out, and_13_out, and_14_out, and_15_out, and_16_out, not_1_out;

  not not_1 (not_1_out, in_17);
  and and_1 (and_1_out, bin0_1, not_1_out);
  and and_2 (and_2_out, bin1_1, not_1_out);
  and and_3 (and_3_out, bin2_1, not_1_out);
  and and_4 (and_4_out, bin3_1, not_1_out);
  and and_5 (and_5_out, bin4_1, not_1_out);
  and and_6 (and_6_out, bin5_1, not_1_out);
  and and_7 (and_7_out, bin6_1, not_1_out);
  and and_8 (and_8_out, bin7_1, not_1_out);
  and and_9 (and_9_out, bin0_2, in_17);
  and and_10 (and_10_out, bin1_2, in_17);
  and and_11 (and_11_out, bin2_2, in_17);
  and and_12 (and_12_out, bin3_2, in_17);
  and and_13 (and_13_out, bin4_2, in_17);
  and and_14 (and_14_out, bin5_2, in_17);
  and and_15 (and_15_out, bin6_2, in_17);
  and and_16 (and_16_out, bin7_2, in_17);
  or or_1 (out_18, and_9_out, and_1_out);
  or or_2 (out_19, and_10_out, and_2_out);
  or or_3 (out_20, and_11_out, and_3_out);
  or or_4 (out_21, and_12_out, and_4_out);
  or or_5 (out_22, and_13_out, and_5_out);
  or or_6 (out_23, and_14_out, and_6_out);
  or or_7 (out_24, and_15_out, and_7_out);
  or or_8 (out_25, and_16_out, and_8_out);
endmodule

module x4p1 (
  input  bin0_1,
  input  bin1_1,
  input  bin2_1,
  input  bin3_1,
  input  bin4_1,
  input  bin5_1,
  input  bin6_1,
  input  bin7_1,
  output out_9,
  output out_10,
  output out_11,
  output out_12,
  output out_13,
  output out_14,
  output out_15,
  output out_16,
  output out_17
);

  wire summator_1_out_19, summator_1_out_20, summator_1_out_21, summator_1_out_22, summator_1_out_23,
       summator_1_out_24, summator_1_out_25, summator_1_out_26, summator_1_out_27, summator_2_out_19,
       summator_2_out_20, summator_2_out_21, summator_2_out_22, summator_2_out_23, summator_2_out_24,
       summator_2_out_25, summator_2_out_26, summator_2_out_27;

  summator summator_1 (
    .bin0_1(bin0_1), .in_3(bin1_1), .bin2_1(bin2_1), .bin3_1(bin3_1), .bin4_1(bin4_1), .bin5_1(bin5_1),
    .bin6_1(bin6_1), .bin7_1(bin7_1), .in_17(1'b0), .bin0_2(bin0_1), .bin1_2(bin1_1), .bin2_2(bin2_1),
    .bin3_2(bin3_1), .bin4_2(bin4_1), .bin5_2(bin5_1), .bin6_2(bin6_1), .bin7_2(bin7_1), .in_18(1'b0),
    .out_19(summator_1_out_19), .out_20(summator_1_out_20), .out_21(summator_1_out_21),
    .out_22(summator_1_out_22), .out_23(summator_1_out_23), .out_24(summator_1_out_24),
    .out_25(summator_1_out_25), .out_26(summator_1_out_26), .out_27(summator_1_out_27));
  summator summator_2 (
    .bin0_1(summator_1_out_19), .in_3(summator_1_out_20), .bin2_1(summator_1_out_21),
    .bin3_1(summator_1_out_22), .bin4_1(summator_1_out_23), .bin5_1(summator_1_out_24),
    .bin6_1(summator_1_out_25), .bin7_1(summator_1_out_26), .in_17(summator_1_out_27),
    .bin0_2(summator_1_out_19), .bin1_2(summator_1_out_20), .bin2_2(summator_1_out_21),
    .bin3_2(summator_1_out_22), .bin4_2(summator_1_out_23), .bin5_2(summator_1_out_24),
    .bin6_2(summator_1_out_25), .bin7_2(summator_1_out_26), .in_18(summator_1_out_27),
    .out_19(summator_2_out_19), .out_20(summator_2_out_20), .out_21(summator_2_out_21),
    .out_22(summator_2_out_22), .out_23(summator_2_out_23), .out_24(summator_2_out_24),
    .out_25(summator_2_out_25), .out_26(summator_2_out_26), .out_27(summator_2_out_27));
  summator summator_3 (
    .bin0_1(summator_2_out_19), .in_3(summator_2_out_20), .bin2_1(summator_2_out_21),
    .bin3_1(summator_2_out_22), .bin4_1(summator_2_out_23), .bin5_1(summator_2_out_24),
    .bin6_1(summator_2_out_25), .bin7_1(summator_2_out_26), .in_17(summator_2_out_27), .bin0_2(1'b1),
    .out_19(out_9), .out_20(out_10), .out_21(out_11), .out_22(out_12), .out_23(out_13), .out_24(out_14),
    .out_25(out_15), .out_26(out_16), .out_27(out_17));  // open: bin1_2, bin2_2, bin3_2, bin4_2, bin5_2, bin6_2, bin7_2, in_18
endmodule

module JKtrigger (
  input  in_1,
  input  in_2,
  input  in_3,
  input  in_4,
  output out_5,
  output out_6
);

  wire and_1_out, and_2_out, not_1_out, rstrigger_2_out_5, rstrigger_2_out_6;

  and and_1 (and_1_out, rstrigger_2_out_5, in_1);
  and and_2 (and_2_out, in_3, rstrigger_2_out_6);
  RStrigger rstrigger_1 (.in_1(and_1_out), .in_2(in_2), .in_3(and_2_out), .in_4(in_4), .out_5(out_5), .out_6(out_6));
  not not_1 (not_1_out, in_2);
  RStrigger rstrigger_2 (
    .in_1(out_6), .in_2(not_1_out), .in_3(out_5), .in_4(in_4), .out_5(rstrigger_2_out_5),
    .out_6(rstrigger_2_out_6));
endmodule
